# Fritzing sketch layout (saved by Fritzing 0.9.3b)
breadboards: 1

parts:
  Componente1 = Arduino Nano (Rev3.0)
  X9C104 = 555 Timer [part_number=X9C104 package="DIP8 [THT]"]
  Input/Output = Audio Jack (TRS) 3.5mm [package="4Ucon 08780 [THT]"]
  Rate = POT [package=pot_mammoth]

nets:
  N1: Componente1.GND, X9C104.Reset, Rate.E
  N2: Componente1.D2, X9C104.Ground
  N3: Componente1.D3, X9C104.Trigger
  N4: Componente1.D4, X9C104.Discharge
  N5: Componente1.5V, X9C104.Vcc_Supply_Voltage, Rate.S
  N6: Componente1.A2, Rate.A
  N7: X9C104.Output, Input/Output.Tip
  N8: X9C104.Control_Voltage, Input/Output.Ring
  N9: X9C104.Threshold, Input/Output.Sleeve
